# Fritzing sketch diy_ac_thermostat (saved by Fritzing 0.8.7b)
breadboards: 1

parts:
  MH-ET_LIVE_ESP32_DEVKIT1 = MH-ET LIVE ESP32 DEVKIT 38 pins
  DHT1 = DHT11 Humitidy and Temperature Sensor
  Mod1 = KY-005 Infrared Transmitter Module [package="Breakout board"]
  R1 = Resistor [package="2512 [SMD]"]  # not connected
  S1 = SWITCH-MOMENTARY-2 [package=tactile_switch_smd-2]
  S2 = SWITCH-MOMENTARY-2 [package=tactile_switch_smd-2]
  TFT1 = Color 320x240 TFT Display, ILI9341 Controller Chip

nets:
  3V3: MH-ET_LIVE_ESP32_DEVKIT1.3V3, DHT1.VDD, Mod1.Vin, TFT1.VCC, TFT1.LED
  N1: MH-ET_LIVE_ESP32_DEVKIT1.RST, TFT1.Reset
  N2: MH-ET_LIVE_ESP32_DEVKIT1.IO32, S2.2
  N3: MH-ET_LIVE_ESP32_DEVKIT1.IO33, S1.1
  N4: MH-ET_LIVE_ESP32_DEVKIT1.GND#58, Mod1.-, S1.2, S2.1
  N5: MH-ET_LIVE_ESP32_DEVKIT1.IO13, TFT1.D/C
  GND: MH-ET_LIVE_ESP32_DEVKIT1.GND#64, DHT1.GND, TFT1.GND
  N6: MH-ET_LIVE_ESP32_DEVKIT1.IO23, TFT1.SDI_(MOSI)
  N7: MH-ET_LIVE_ESP32_DEVKIT1.IO19, TFT1.SDO_(MISO)
  N8: MH-ET_LIVE_ESP32_DEVKIT1.IO18, TFT1.SCK
  N9: MH-ET_LIVE_ESP32_DEVKIT1.IO5, DHT1.DATA
  N10: MH-ET_LIVE_ESP32_DEVKIT1.IO4, Mod1.S
  N11: MH-ET_LIVE_ESP32_DEVKIT1.IO15, TFT1.CS

custom parts:
  MH-ET LIVE ESP32 DEVKIT 38 pins: http://mh.nodebb.com/topic/2/mh-et-live-esp32-devkit
  DHT11 Humitidy and Temperature Sensor: DHT11 Humidity and Temperature Sensor
  KY-005 Infrared Transmitter Module: Arduino IR Transmitter Module Keyes KY-005, emits infrared light at 38KHz.
  Color 320x240 TFT Display, ILI9341 Controller Chip: 2.2" TFT Display with ILI9341 Controller
